# Fritzing sketch orbino (saved by Fritzing 0.8.7b)
circuit board: 8.46667cm x 5.64444cm
breadboards: 1

parts:
  Composant2 = Arduino Ethernet Shield (Rev3)
  R1 = Resistor [tolerance=±5% resistance=330 package=THT]
  R2 = Resistor [tolerance=±5% resistance=330 package=THT]
  R3 = Resistor [tolerance=±5% resistance=330 package=THT]
  LED1 = RGB LED (com. anode, rbg) [package="5 mm [THT]"]

nets:
  N1: Composant2.GND, LED1.common_anode
  N2: Composant2.PWM_D3, R2.Pin_1
  N3: Composant2.PWM_D5, R3.Pin_1
  N4: Composant2.PWM_D6, R1.Pin_1
  N5: R1.Pin_0, LED1.green_cathode
  N6: R2.Pin_0, LED1.red_cathode
  N7: R3.Pin_0, LED1.blue_cathode
